# Fritzing sketch teste (saved by Fritzing 0.9.6b)
circuit board: 8.46667cm x 5.64444cm
breadboards: 2

parts:
  Componente1 = Franzininho WiFi
  R1 = Resistor [tolerance=±5% power=0.25 resistance=220 package=THT]
  LED1 = LED - 5mm [color="Red (633nm)" current=0.030 package="5 mm [THT]"]

nets:
  N1: Componente1.9, R1.Pin_0
  N2: Componente1.GND, LED1.cathode
  N3: R1.Pin_1, LED1.anode

custom parts:
  Franzininho WiFi: Placa de desenvolvimento ESP32-S2
